# Fritzing sketch Sketch (saved by Fritzing 0.9.4)
breadboards: 1

parts:
  MH-ET_LIVE_ESP32_DEVKIT1 = MH-ET LIVE ESP32 DEVKIT 38 pins
  Component1 = RS485_XY-017 [part_number=XY-017]
  OLED1 = OLED 128x64 I2C Monochrome Display
  M1 = SN65HVD230 CAN Bus transciever module [package=THT]
  Component2 = RS485_XY-017 [part_number=XY-017]

nets:
  N1: MH-ET_LIVE_ESP32_DEVKIT1.IO22, OLED1.SCK
  N2: MH-ET_LIVE_ESP32_DEVKIT1.IO21, OLED1.SDA
  N3: MH-ET_LIVE_ESP32_DEVKIT1.IO19, Component1.RXD
  N4: MH-ET_LIVE_ESP32_DEVKIT1.IO18, Component1.TXD
  N5: MH-ET_LIVE_ESP32_DEVKIT1.IO5, M1.pin_3
  N6: MH-ET_LIVE_ESP32_DEVKIT1.IO4, M1.pin_4
  GND: Component1.GND, OLED1.GND, M1.pin_2, Component2.GND
  VCC: Component1.VCC, OLED1.VDD, M1.pin_1, Component2.VCC

custom parts:
  MH-ET LIVE ESP32 DEVKIT 38 pins: http://mh.nodebb.com/topic/2/mh-et-live-esp32-devkit
  RS485_XY-017: Commercially available RS485 to RS232 TTL Module
  SN65HVD230 CAN Bus transciever module: Bus Transceiver SN65HVD230 CAN Communication Module, for Arduino.
